// Logisim project Guoyanduo.circ as structural Verilog: 5 circuits, main circuit main
module main (
  output [15:0] out_1,
  output [15:0] out_2,
  output [15:0] out_3,
  output [15:0] out_4
);

  wire addi_out, and_7_out, and_8_out, and_9_out, and_10_out, and_11_out, and_12_out, and_13_out, and_14_out,
       and_30_out, and_31_out, and_32_out, and_33_out, andi_out, clk, not_1_out, not_2_out, not_3_out,
       not_4_out, not_5_out, not_6_out, not_7_out, not_8_out, not_9_out, not_10_out, not_11_out, not_12_out,
       not_13_out, not_14_out, not_15_out, not_16_out, not_17_out, not_18_out, not_19_out, not_20_out,
       not_21_out, not_22_out, or_1_out, or_6_out, ori_out, R0, R1, R2, R3;
  wire [1:0] and_1_out, and_2_out, bit_extender_1_out, bit_extender_2_out, or_2_out;
  wire [15:0] alu_add_1_out_3, alu_add_2_out_3, alu_add_3_out_3, alu_sub_1_rd, and_15_out, and_16_out,
       and_17_out, and_18_out, and_19_out, and_20_out, and_21_out, and_22_out, and_23_out, and_24_out,
       and_25_out, and_26_out, and_27_out, and_28_out, and_29_out, and_34_out, and_35_out, and_36_out,
       and_37_out, bit_extender_3_out, bit_extender_4_out, bit_extender_5_out, bit_extender_6_out,
       bit_extender_7_out, bit_extender_8_out, bit_extender_9_out, bit_extender_10_out, bit_extender_11_out,
       bit_extender_12_out, bit_extender_13_out, bit_extender_14_out, bit_extender_15_out,
       bit_extender_16_out, bit_extender_17_out, bit_extender_18_out, bit_extender_19_out, fullimm, or_3_out,
       or_4_out, or_7_out, or_8_out, PC_q, R0out, R1out, R2out, rsOUT, rtOUT;

  Clock clock_1 (.out(clk));
  or or_1 (or_1_out, out_1[15], out_1[14], out_1[13], out_1[12]);
  Register #(.width(16)) PC (.D(alu_add_1_out_3), .clk(clk), .Q(PC_q));  // open: en, clr
  not not_1 (not_1_out, or_1_out);
  ROM #(.addrWidth(16), .dataWidth(16)) mem (.addr(PC_q), .data(out_1));
  assign bit_extender_1_out = {{1{not_1_out}}, not_1_out};  // Bit_Extender bit_extender_1
  assign and_1_out = bit_extender_1_out & {out_1[6], out_1[7]};  // AND_Gate and_1, 2 bits wide
  assign bit_extender_2_out = {{1{or_1_out}}, or_1_out};  // Bit_Extender bit_extender_2
  Register #(.width(16)) u_R0 (.D(out_2), .en(R0), .clk(clk), .Q(R0out));  // open: clr
  Register #(.width(16)) u_R1 (.D(out_2), .en(R1), .clk(clk), .Q(R1out));  // open: clr
  Register #(.width(16)) u_R2 (.D(out_2), .en(R2), .clk(clk), .Q(R2out));  // open: clr
  Register #(.width(16)) u_R3 (.D(out_2), .en(R3), .clk(clk), .Q(out_3));  // open: clr
  assign and_2_out = bit_extender_2_out & {out_1[8], out_1[9]};  // AND_Gate and_2, 2 bits wide
  ALU_ADD alu_add_1 (.A(16'h1), .B(PC_q), .out_3(alu_add_1_out_3));
  assign or_2_out = and_1_out | and_2_out;  // OR_Gate or_2, 2 bits wide
  not not_2 (not_2_out, or_2_out[0]);
  not not_3 (not_3_out, or_2_out[1]);
  not not_4 (not_4_out, or_2_out[0]);
  not not_5 (not_5_out, or_2_out[1]);
  and and_3 (R0, not_2_out, not_3_out);
  and and_4 (R1, not_4_out, or_2_out[1]);
  and and_5 (R2, or_2_out[0], not_5_out);
  and and_6 (R3, or_2_out[0], or_2_out[1]);
  expander expander_1 (.imm(out_1[7:0]), .opcode({out_1[12], out_1[13], out_1[14], out_1[15]}), .immout(fullimm));
  not not_6 (not_6_out, out_1[9]);
  not not_7 (not_7_out, out_1[8]);
  not not_8 (not_8_out, out_1[9]);
  not not_9 (not_9_out, out_1[8]);
  and and_7 (and_7_out, not_6_out, not_7_out);
  and and_8 (and_8_out, not_8_out, out_1[8]);
  and and_9 (and_9_out, out_1[9], not_9_out);
  and and_10 (and_10_out, out_1[9], out_1[8]);
  not not_10 (not_10_out, out_1[1]);
  not not_11 (not_11_out, out_1[0]);
  not not_12 (not_12_out, out_1[1]);
  not not_13 (not_13_out, out_1[0]);
  and and_11 (and_11_out, not_10_out, not_11_out);
  and and_12 (and_12_out, not_12_out, out_1[0]);
  and and_13 (and_13_out, out_1[1], not_13_out);
  and and_14 (and_14_out, out_1[1], out_1[0]);
  not not_14 (not_14_out, out_1[14]);
  not not_15 (not_15_out, out_1[13]);
  not not_16 (not_16_out, out_1[12]);
  not not_17 (not_17_out, out_1[13]);
  assign bit_extender_3_out = {{15{and_7_out}}, and_7_out};  // Bit_Extender bit_extender_3
  assign bit_extender_4_out = {{15{and_8_out}}, and_8_out};  // Bit_Extender bit_extender_4
  assign bit_extender_5_out = {{15{and_9_out}}, and_9_out};  // Bit_Extender bit_extender_5
  assign bit_extender_6_out = {{15{and_10_out}}, and_10_out};  // Bit_Extender bit_extender_6
  and ori (ori_out, out_1[12], out_1[13], not_14_out);
  and addi (addi_out, out_1[14], not_15_out, not_16_out);
  and andi (andi_out, out_1[12], not_17_out, out_1[14]);
  assign or_3_out = rsOUT | rtOUT;  // OR_Gate or_3, 16 bits wide
  assign bit_extender_7_out = {{15{and_11_out}}, and_11_out};  // Bit_Extender bit_extender_7
  assign bit_extender_8_out = {{15{ori_out}}, ori_out};  // Bit_Extender bit_extender_8
  assign bit_extender_9_out = {{15{addi_out}}, addi_out};  // Bit_Extender bit_extender_9
  assign and_15_out = R0out & bit_extender_3_out;  // AND_Gate and_15, 16 bits wide
  assign and_16_out = R1out & bit_extender_4_out;  // AND_Gate and_16, 16 bits wide
  assign and_17_out = R2out & bit_extender_5_out;  // AND_Gate and_17, 16 bits wide
  assign and_18_out = out_3 & bit_extender_6_out;  // AND_Gate and_18, 16 bits wide
  assign bit_extender_10_out = {{15{and_12_out}}, and_12_out};  // Bit_Extender bit_extender_10
  assign bit_extender_11_out = {{15{and_13_out}}, and_13_out};  // Bit_Extender bit_extender_11
  assign bit_extender_12_out = {{15{and_14_out}}, and_14_out};  // Bit_Extender bit_extender_12
  assign bit_extender_13_out = {{15{andi_out}}, andi_out};  // Bit_Extender bit_extender_13
  assign and_19_out = or_3_out & bit_extender_7_out;  // AND_Gate and_19, 16 bits wide
  assign and_20_out = rsOUT & rtOUT;  // AND_Gate and_20, 16 bits wide
  ALU_ADD alu_add_2 (.A(rsOUT), .B(rtOUT), .out_3(alu_add_2_out_3));
  ALU_SUB alu_sub_1 (.rs(rsOUT), .rt(rtOUT), .rd(alu_sub_1_rd));
  assign or_4_out = fullimm | rsOUT;  // OR_Gate or_4, 16 bits wide
  ALU_ADD alu_add_3 (.A(fullimm), .B(rsOUT), .out_3(alu_add_3_out_3));
  assign and_21_out = rsOUT & fullimm;  // AND_Gate and_21, 16 bits wide
  assign and_22_out = and_20_out & bit_extender_10_out;  // AND_Gate and_22, 16 bits wide
  assign and_23_out = alu_add_2_out_3 & bit_extender_11_out;  // AND_Gate and_23, 16 bits wide
  assign and_24_out = alu_sub_1_rd & bit_extender_12_out;  // AND_Gate and_24, 16 bits wide
  assign and_25_out = or_4_out & bit_extender_8_out;  // AND_Gate and_25, 16 bits wide
  assign and_26_out = alu_add_3_out_3 & bit_extender_9_out;  // AND_Gate and_26, 16 bits wide
  assign and_27_out = and_21_out & bit_extender_13_out;  // AND_Gate and_27, 16 bits wide
  assign rtOUT = and_15_out | and_16_out | and_17_out | and_18_out;  // OR_Gate or_5, 16 bits wide
  or or_6 (or_6_out, out_1[15], out_1[14], out_1[13], out_1[12]);
  not not_18 (not_18_out, or_6_out);
  assign or_7_out = and_19_out | and_22_out | and_23_out | and_24_out;  // OR_Gate or_7, 16 bits wide
  assign bit_extender_14_out = {{15{or_6_out}}, or_6_out};  // Bit_Extender bit_extender_14
  assign bit_extender_15_out = {{15{not_18_out}}, not_18_out};  // Bit_Extender bit_extender_15
  assign or_8_out = and_25_out | and_26_out | and_27_out;  // OR_Gate or_8, 16 bits wide
  assign and_28_out = bit_extender_15_out & or_7_out;  // AND_Gate and_28, 16 bits wide
  assign and_29_out = or_8_out & bit_extender_14_out;  // AND_Gate and_29, 16 bits wide
  not not_19 (not_19_out, out_1[11]);
  not not_20 (not_20_out, out_1[10]);
  not not_21 (not_21_out, out_1[11]);
  not not_22 (not_22_out, out_1[10]);
  assign out_2 = and_28_out | and_29_out;  // OR_Gate or_9, 16 bits wide
  and and_30 (and_30_out, not_19_out, not_20_out);
  and and_31 (and_31_out, not_21_out, out_1[10]);
  and and_32 (and_32_out, out_1[11], not_22_out);
  and and_33 (and_33_out, out_1[11], out_1[10]);
  assign bit_extender_16_out = {{15{and_30_out}}, and_30_out};  // Bit_Extender bit_extender_16
  assign bit_extender_17_out = {{15{and_31_out}}, and_31_out};  // Bit_Extender bit_extender_17
  assign bit_extender_18_out = {{15{and_32_out}}, and_32_out};  // Bit_Extender bit_extender_18
  assign bit_extender_19_out = {{15{and_33_out}}, and_33_out};  // Bit_Extender bit_extender_19
  assign and_34_out = R0out & bit_extender_16_out;  // AND_Gate and_34, 16 bits wide
  assign and_35_out = R1out & bit_extender_17_out;  // AND_Gate and_35, 16 bits wide
  assign and_36_out = R2out & bit_extender_18_out;  // AND_Gate and_36, 16 bits wide
  assign and_37_out = out_3 & bit_extender_19_out;  // AND_Gate and_37, 16 bits wide
  assign rsOUT = and_34_out | and_35_out | and_36_out | and_37_out;  // OR_Gate or_10, 16 bits wide

  // Other names for the same wires on the sheet: funct[2:0] = {out_1[0], out_1[1], out_1[2]}; imm[7:0] = out_1[7:0];
  //   rd[1:0] = {out_1[6], out_1[7]}; opcode[3:0] = {out_1[12], out_1[13], out_1[14], out_1[15]}; R3out[15:0] = out_3;
  //   RegIn[15:0] = out_2; rs[1:0] = {out_1[10], out_1[11]}; rt[1:0] = {out_1[8], out_1[9]}

  // Notes on the sheet:
  //   contents of mem (hex, n*v repeats v):
  //   e42 b01 b03 d80 4c08 588*0 111 0 0 0 101
endmodule

module ALU_ADD (
  input  [15:0] A,
  input  [15:0] B,
  output [15:0] out_3
);

  wire onebitadder_1_up, onebitadder_2_up, onebitadder_3_up, onebitadder_4_up, onebitadder_5_up,
       onebitadder_6_up, onebitadder_7_up, onebitadder_8_up, onebitadder_9_up, onebitadder_10_up,
       onebitadder_11_up, onebitadder_12_up, onebitadder_13_up, onebitadder_14_up, onebitadder_15_up;

  oneBitAdder onebitadder_1 (.a(A[0]), .b(B[0]), .isup(1'b0), .RES(out_3[0]), .UP(onebitadder_1_up));
  oneBitAdder onebitadder_2 (.a(A[1]), .b(B[1]), .isup(onebitadder_1_up), .RES(out_3[1]), .UP(onebitadder_2_up));
  oneBitAdder onebitadder_3 (.a(A[2]), .b(B[2]), .isup(onebitadder_2_up), .RES(out_3[2]), .UP(onebitadder_3_up));
  oneBitAdder onebitadder_4 (.a(A[3]), .b(B[3]), .isup(onebitadder_3_up), .RES(out_3[3]), .UP(onebitadder_4_up));
  oneBitAdder onebitadder_5 (.a(A[4]), .b(B[4]), .isup(onebitadder_4_up), .RES(out_3[4]), .UP(onebitadder_5_up));
  oneBitAdder onebitadder_6 (.a(A[5]), .b(B[5]), .isup(onebitadder_5_up), .RES(out_3[5]), .UP(onebitadder_6_up));
  oneBitAdder onebitadder_7 (.a(A[6]), .b(B[6]), .isup(onebitadder_6_up), .RES(out_3[6]), .UP(onebitadder_7_up));
  oneBitAdder onebitadder_8 (.a(A[7]), .b(B[7]), .isup(onebitadder_7_up), .RES(out_3[7]), .UP(onebitadder_8_up));
  oneBitAdder onebitadder_9 (.a(A[8]), .b(B[8]), .isup(onebitadder_8_up), .RES(out_3[8]), .UP(onebitadder_9_up));
  oneBitAdder onebitadder_10 (.a(A[9]), .b(B[9]), .isup(onebitadder_9_up), .RES(out_3[9]), .UP(onebitadder_10_up));
  oneBitAdder onebitadder_11 (.a(A[10]), .b(B[10]), .isup(onebitadder_10_up), .RES(out_3[10]), .UP(onebitadder_11_up));
  oneBitAdder onebitadder_12 (.a(A[11]), .b(B[11]), .isup(onebitadder_11_up), .RES(out_3[11]), .UP(onebitadder_12_up));
  oneBitAdder onebitadder_13 (.a(A[12]), .b(B[12]), .isup(onebitadder_12_up), .RES(out_3[12]), .UP(onebitadder_13_up));
  oneBitAdder onebitadder_14 (.a(A[13]), .b(B[13]), .isup(onebitadder_13_up), .RES(out_3[13]), .UP(onebitadder_14_up));
  oneBitAdder onebitadder_15 (.a(A[14]), .b(B[14]), .isup(onebitadder_14_up), .RES(out_3[14]), .UP(onebitadder_15_up));
  oneBitAdder onebitadder_16 (.a(A[15]), .b(B[15]), .isup(onebitadder_15_up), .RES(out_3[15]));  // open: UP
endmodule

module oneBitAdder (
  input  a,
  input  b,
  input  isup,
  output RES,
  output UP
);

  wire and_1_out, and_2_out, and_3_out, or_1_out, xor_1_out;

  and and_1 (and_1_out, a, isup);
  and and_2 (and_2_out, b, isup);
  and and_3 (and_3_out, a, b);
  or or_1 (or_1_out, and_2_out, and_1_out);
  xor xor_1 (xor_1_out, a, b);
  or or_2 (UP, and_3_out, or_1_out);
  xor xor_2 (RES, xor_1_out, isup);
endmodule

module ALU_SUB (
  input  [15:0] rs,
  input  [15:0] rt,
  output [15:0] rd
);

  wire [15:0] alu_add_1_out_3, xor_1_out;

  assign xor_1_out = rt ^ {16{1'b1}};  // XOR_Gate xor_1, 16 bits wide
  ALU_ADD alu_add_1 (.A(xor_1_out), .B(16'h1), .out_3(alu_add_1_out_3));
  ALU_ADD alu_add_2 (.A(rs), .B(alu_add_1_out_3), .out_3(rd));
endmodule

module expander (
  input  [7:0] imm,
  input  [3:0] opcode,
  output [15:0] immout
);

  wire not_1_out, not_2_out;

  not not_1 (not_1_out, opcode[1]);
  not not_2 (not_2_out, opcode[0]);
  and and_1 (immout[15], opcode[2], not_1_out, not_2_out);

  assign immout[14:0] = {{7{immout[15]}}, imm};
endmodule
